// Logisim project Modules.circ as structural Verilog: 5 circuits, main circuit main
module main (
  input  [9:0] in_1,
  input  [9:0] in_2,
  input  in_3,
  output out_4
);

  _10_bit_MUX_module u_10_bit_mux_module_1 (
    .SELECTION(in_3), .A(in_2), .B(in_1), ._0(out_4));  // open: _1, _2, _3, _4, _5, _6, _7, _8, _9
endmodule

module _4_bit_MUX_module (
  input  A0,
  input  A1,
  input  A2,
  input  A3,
  input  B0,
  input  B1,
  input  B2,
  input  B3,
  input  SELECTION,
  output _0,
  output _1,
  output _2,
  output _3
);

  // _74157 74157_1: pin names not known; wires that end beside it: SELECTION, A0, B0, _0, A1, B1, _1, 1'b0, 1'b1, 1'b0, A3, B3, _3, A2, B2, _2
endmodule

module _2_bit_MUX_module (
  input  A0,
  input  A1,
  input  B0,
  input  B1,
  input  SELECTION,
  output out_6,
  output out_7
);

  // _74157 74157_1: pin names not known; wires that end beside it: SELECTION, A0, B0, out_6, A1, B1, out_7, 1'b0, 1'b1, 1'b0, 1'b0
endmodule

module _10_bit_MUX_module (
  input  [9:0] B,
  input  SELECTION,
  input  [9:0] A,
  output _7,
  output _8,
  output _4,
  output _5,
  output _6,
  output _9,
  output _0,
  output _1,
  output _2,
  output _3
);

  _4_bit_MUX_module u_4_bit_mux_module_1 (
    .SELECTION(SELECTION), .A0(A[0]), .A1(A[1]), .A2(A[2]), .A3(A[3]), .B0(B[0]), .B1(B[1]), .B2(B[2]),
    .B3(B[3]), ._0(_0), ._1(_1), ._2(_2), ._3(_3));
  _4_bit_MUX_module u_4_bit_mux_module_2 (
    .SELECTION(SELECTION), .A0(A[4]), .A1(A[5]), .A2(A[6]), .A3(A[7]), .B0(B[4]), .B1(B[5]), .B2(B[6]),
    .B3(B[7]), ._0(_4), ._1(_5), ._2(_6), ._3(_7));
  _2_bit_MUX_module u_2_bit_mux_module_1 (
    .SELECTION(SELECTION), .A0(A[8]), .A1(A[9]), .B0(B[8]), .B1(B[9]), .out_6(_8), .out_7(_9));

  // Notes on the sheet:
  //   A
endmodule

module _22_bit_MUX_module (
  input  [21:0] B,
  input  [21:0] A,
  input  Selection,
  output _4,
  output _5,
  output _6,
  output _7,
  output _0,
  output _1,
  output _2,
  output _8,
  output _9,
  output _10,
  output _11,
  output _12,
  output _13,
  output _14,
  output _15,
  output _16,
  output _17,
  output _18,
  output _19,
  output _20,
  output _21,
  output _3
);

  _4_bit_MUX_module u_4_bit_mux_module_1 (
    .SELECTION(Selection), .A0(A[0]), .A1(A[1]), .A2(A[2]), .A3(A[3]), .B0(B[0]), .B1(B[1]), .B2(B[2]),
    .B3(B[3]), ._0(_0), ._1(_1), ._2(_2), ._3(_3));
  _4_bit_MUX_module u_4_bit_mux_module_2 (
    .SELECTION(Selection), .A0(A[4]), .A1(A[5]), .A2(A[6]), .A3(A[7]), .B0(B[4]), .B1(B[5]), .B2(B[6]),
    .B3(B[7]), ._0(_4), ._1(_5), ._2(_6), ._3(_7));
  _4_bit_MUX_module u_4_bit_mux_module_3 (
    .SELECTION(Selection), .A0(A[8]), .A1(A[9]), .A2(A[10]), .A3(A[11]), .B0(B[8]), .B1(B[9]), .B2(B[10]),
    .B3(B[11]), ._0(_8), ._1(_9), ._2(_10), ._3(_11));
  _4_bit_MUX_module u_4_bit_mux_module_4 (
    .SELECTION(Selection), .A0(A[12]), .A1(A[13]), .A2(A[14]), .A3(A[15]), .B0(B[12]), .B1(B[13]),
    .B2(B[14]), .B3(B[15]), ._0(_12), ._1(_13), ._2(_14), ._3(_15));
  _4_bit_MUX_module u_4_bit_mux_module_5 (
    .SELECTION(Selection), .A0(A[16]), .A1(A[17]), .A2(A[18]), .A3(A[19]), .B0(B[16]), .B1(B[17]),
    .B2(B[18]), .B3(B[19]), ._0(_16), ._1(_17), ._2(_18), ._3(_19));
  _2_bit_MUX_module u_2_bit_mux_module_1 (
    .SELECTION(Selection), .A0(A[20]), .A1(A[21]), .B0(B[20]), .B1(B[21]), .out_6(_20), .out_7(_21));
endmodule
