// Logisim project Register_Memory.circ as structural Verilog: 1 circuit, main circuit Register Memory
module Register_Memory (
  input  [3:0] Read_1_Address,
  input  [3:0] Write_Data,
  input  RegWrite,
  input  CLK,
  input  [3:0] Write_Address,
  input  [3:0] Read_2_Address,
  output [3:0] Read_1_Data,
  output [3:0] Read_2_Data
);

  wire and_1_out, demultiplexer_1_out0, demultiplexer_1_out1, demultiplexer_1_out2, demultiplexer_1_out3,
       demultiplexer_1_out4;
  wire [3:0] t0_q, t1_q, t2_q, t3_q, t4_q, zero_q;

  Demultiplexer #(.select(3), .enable("false")) demultiplexer_1 (
    .out0(demultiplexer_1_out0), .out1(demultiplexer_1_out1), .out2(demultiplexer_1_out2),
    .out3(demultiplexer_1_out3), .out4(demultiplexer_1_out4), .in(and_1_out), .sel(Write_Address[2:0]));  // open: out5, out6, out7
  and and_1 (and_1_out, RegWrite, CLK);
  Register #(.width(4)) zero (.D(4'b0000), .Q(zero_q), .clk(1'b0));  // open: en, clr
  Register #(.width(4)) t0 (.D(Write_Data), .Q(t0_q), .clk(demultiplexer_1_out0));  // open: en, clr
  Register #(.width(4)) t1 (.D(Write_Data), .Q(t1_q), .clk(demultiplexer_1_out1));  // open: en, clr
  Register #(.width(4)) t2 (.D(Write_Data), .Q(t2_q), .clk(demultiplexer_1_out2));  // open: en, clr
  Register #(.width(4)) t3 (.D(Write_Data), .Q(t3_q), .clk(demultiplexer_1_out3));  // open: en, clr
  Register #(.width(4)) t4 (.D(Write_Data), .Q(t4_q), .clk(demultiplexer_1_out4));  // open: en, clr
  Multiplexer #(.select(3), .width(4), .enable("false")) multiplexer_1 (
    .in0(t0_q), .in1(t1_q), .in2(t2_q), .in3(t3_q), .in4(t4_q), .in7(zero_q), .out(Read_1_Data),
    .sel(Read_1_Address[2:0]));  // open: in5, in6
  Multiplexer #(.select(3), .width(4), .enable("false")) multiplexer_2 (
    .in0(t0_q), .in1(t1_q), .in2(t2_q), .in3(t3_q), .in4(t4_q), .in7(zero_q), .out(Read_2_Data),
    .sel(Read_2_Address[2:0]));  // open: in5, in6
endmodule
